// Logisim project a.circ as structural Verilog: 1 circuit, main circuit main
// aoeu
module main (
  input  [4:0] in_1,
  output [4:0] out_2
);

  // AND_Gate and_1 is placed but not wired

  assign out_2 = in_1;
endmodule
